# Fritzing sketch FruitMachineReels (saved by Fritzing 0.9.3b)

parts:
  Mod5 = KY-010 Photo Interrupter Module [package="Breakout board"]
  M1 = Stepper Motor - Unipolar
  LED1 = LED - 5mm [color="White (4500K)" package="5 mm [THT]"]
  LED2 = LED - 5mm [color="White (4500K)" package="5 mm [THT]"]
  LED3 = LED - 5mm [color="White (4500K)" package="5 mm [THT]"]
  J1 = female pin header, 15 pins [form="♀ (female)"]
  R1 = Resistor [tolerance=±5% resistance=220 package=THT]

nets:
  N1: Mod5.-, J1.pin11
  N2: Mod5.Vin, R1.Pin_0
  N3: Mod5.S, J1.pin10
  N4: M1.A, J1.pin3
  N5: M1.COMMON_1, J1.pin1
  N6: M1.C, J1.pin4
  N7: M1.B, J1.pin5
  N8: M1.COMMON_2, J1.pin2
  N9: M1.D, J1.pin6
  N10: LED1.cathode, LED2.cathode, LED3.cathode, J1.pin15
  N11: LED1.anode, J1.pin12
  N12: LED2.anode, J1.pin13
  N13: LED3.anode, J1.pin14
  N14: J1.pin9, R1.Pin_1

notes:
  1. Common A (unused) (Green)
  2. Common B (unused) (Green)
  3. A1 (Red)
  4. A2 (Yellow)
  5. B1 (Blue)
  6. B2 (Black)
  7. N/C
  8. N/C
  9. 5V Opto Vin (Pink) - NEEDS CURRENT LIMITING RESISTOR!
  10. Signal Opto (Brown)
  11. Opto GND (Purple/Blue)
  12. Hi Lamp 12V
  13. Mid Lamp 12V
  14. Low Lamp 12V
  15. GND Lamps
  Opto Sensor out goes HIGH when obstructed.
  See:
  https://omronfs.omron.com/en_US/ecb/products/pdf/en-ee_sx4235a_p2_discon.pdf
  https://omronfs.omron.com/en_US/ecb/products/pdf/en-ph_technical.pdf
  Lamps share a common ground, and separately switched +12V
  Unipolar stepper motor (normally 12V, sometimes 24V) has 6 wires (2 sets of 3), but it is not necessary to use the common wire of each pair

custom parts:
  KY-010 Photo Interrupter Module: KY-010 Photo Interrupter Module, it will trigger a signal when light between the sensor's gap is blocked.
